// Logisim project alu.circ as structural Verilog: 4 circuits, main circuit main
module main (
  input  [31:0] X,
  input  [31:0] Y,
  input  [5:0] Switch__S,
  output Signed_Overflow,
  output [31:0] RESULT,
  output Equal
);

  wire comparator_1_eq, not_1_out;
  wire [3:0] bit_extender_5_out;
  wire [4:0] bit_extender_1_out, bit_extender_4_out;
  wire [14:0] bit_extender_2_out;
  wire [16:0] bit_extender_3_out;
  wire [31:0] adder_1_out, and_1_out, divider_1_out, multiplexer_1_out, multiplier_1_out, or_1_out,
       reverse_output, shifter_1_out, subtractor_1_out, u_ls_1_p3, xor_1_out;

  // u_LS u_ls_1: pin names not known; wires that end beside it: X, Y, u_ls_1_p3
  Bit_Extender #(.in_width(32), .out_width(5)) bit_extender_1 (.in(Y), .out(bit_extender_1_out));
  Bit_Extender #(.in_width(32), .out_width(15)) bit_extender_2 (.in(X), .out(bit_extender_2_out));
  Bit_Extender #(.in_width(32), .out_width(17)) bit_extender_3 (.in(Y), .out(bit_extender_3_out));
  Shifter #(.width(32), .shift("ar")) shifter_1 (.in(X), .\dist (bit_extender_1_out), .out(shifter_1_out));
  assign and_1_out = X & Y;  // AND_Gate and_1, 32 bits wide
  assign or_1_out = X | Y;  // OR_Gate or_1, 32 bits wide
  Bit_Extender #(.in_width(32), .out_width(5)) bit_extender_4 (.in(Y), .out(bit_extender_4_out));
  u_REV reverse (.INPUT(X), .REVERSE_AMOUNT(bit_extender_4_out), .OUTPUT(reverse_output));
  assign xor_1_out = X ^ Y;  // XOR_Gate xor_1, 32 bits wide
  Adder #(.width(32)) adder_1 (.a(X), .b(Y), .out(adder_1_out));  // open: cin, cout
  Subtractor #(.width(32)) subtractor_1 (.a(X), .b(Y), .out(subtractor_1_out));  // open: bin, bout
  Multiplier #(.width(32)) multiplier_1 (.a(X), .b(Y), .out(multiplier_1_out));  // open: cin, cout
  Divider #(.width(32)) divider_1 (.a(X), .b(Y), .out(divider_1_out));  // open: upper, rem
  Comparator #(.width(32)) comparator_1 (.a(Y), .b({32{1'b0}}), .eq(comparator_1_eq));  // open: gt, lt
  Multiplexer #(.width(32)) multiplexer_1 (
    .in0(32'h7fffffff), .in1(divider_1_out), .out(multiplexer_1_out), .sel(not_1_out));  // open: en
  not not_1 (not_1_out, comparator_1_eq);
  Multiplexer #(.select(4), .width(32)) multiplexer_2 (
    .in0(u_ls_1_p3), .in1(shifter_1_out), .in2(and_1_out), .in3(or_1_out), .in4(reverse_output),
    .in5(xor_1_out), .in6(adder_1_out), .in7(subtractor_1_out), .in8(multiplier_1_out),
    .in9(multiplexer_1_out), .in10(adder_1_out), .in11(adder_1_out), .in12(adder_1_out), .in13(adder_1_out),
    .in14({bit_extender_3_out, bit_extender_2_out}), .out(RESULT), .sel(bit_extender_5_out));  // open: in15, en
  Bit_Extender #(.in_width(6), .out_width(4)) bit_extender_5 (.in(Switch__S), .out(bit_extender_5_out));

  // Other names for the same wires on the sheet: tunnel = Equal

  // Notes on the sheet:
  //   INPUTS to your circuit
  //   DON'T CHANGE THE INPUTS AND OUTPUTS! IF YOU DO SO, YOU NEED TO MAKE SURE THE PINS ARE IN THE RIGHT PLACES!
  //   INPUT to your circuit
  //   OUTPUTS of your circuit
endmodule

module u_REV (
  input  [31:0] INPUT,
  input  [4:0] REVERSE_AMOUNT,
  output [31:0] OUTPUT
);

  wire [31:0] demultiplexer_1_out0, demultiplexer_1_out1, demultiplexer_2_out0, demultiplexer_2_out1,
       demultiplexer_3_out0, demultiplexer_3_out1, demultiplexer_4_out0, demultiplexer_4_out1,
       demultiplexer_5_out0, demultiplexer_5_out1, multiplexer_1_out, multiplexer_2_out, multiplexer_3_out,
       multiplexer_4_out;

  Demultiplexer #(.width(32)) demultiplexer_1 (
    .out0(demultiplexer_1_out0), .out1(demultiplexer_1_out1), .in(INPUT), .sel(REVERSE_AMOUNT[0]));  // open: en
  Demultiplexer #(.width(32)) demultiplexer_2 (
    .out0(demultiplexer_2_out0), .out1(demultiplexer_2_out1), .in(multiplexer_1_out), .sel(REVERSE_AMOUNT[1]));  // open: en
  Multiplexer #(.width(32)) multiplexer_1 (
    .in0(demultiplexer_1_out0),
    .in1({demultiplexer_1_out1[30], demultiplexer_1_out1[31], demultiplexer_1_out1[28], demultiplexer_1_out1[29], demultiplexer_1_out1[26], demultiplexer_1_out1[27], demultiplexer_1_out1[24], demultiplexer_1_out1[25], demultiplexer_1_out1[22], demultiplexer_1_out1[23], demultiplexer_1_out1[20], demultiplexer_1_out1[21], demultiplexer_1_out1[18], demultiplexer_1_out1[19], demultiplexer_1_out1[16], demultiplexer_1_out1[17], demultiplexer_1_out1[14], demultiplexer_1_out1[15], demultiplexer_1_out1[12], demultiplexer_1_out1[13], demultiplexer_1_out1[10], demultiplexer_1_out1[11], demultiplexer_1_out1[8], demultiplexer_1_out1[9], demultiplexer_1_out1[6], demultiplexer_1_out1[7], demultiplexer_1_out1[4], demultiplexer_1_out1[5], demultiplexer_1_out1[2], demultiplexer_1_out1[3], demultiplexer_1_out1[0], demultiplexer_1_out1[1]}),
    .out(multiplexer_1_out), .sel(REVERSE_AMOUNT[0]));  // open: en
  Multiplexer #(.width(32)) multiplexer_2 (
    .in0(demultiplexer_2_out0),
    .in1({demultiplexer_2_out1[29:28], demultiplexer_2_out1[31:30], demultiplexer_2_out1[25:24], demultiplexer_2_out1[27:26], demultiplexer_2_out1[21:20], demultiplexer_2_out1[23:22], demultiplexer_2_out1[17:16], demultiplexer_2_out1[19:18], demultiplexer_2_out1[13:12], demultiplexer_2_out1[15:14], demultiplexer_2_out1[9:8], demultiplexer_2_out1[11:10], demultiplexer_2_out1[5:4], demultiplexer_2_out1[7:6], demultiplexer_2_out1[1:0], demultiplexer_2_out1[3:2]}),
    .out(multiplexer_2_out), .sel(REVERSE_AMOUNT[1]));  // open: en
  Demultiplexer #(.width(32)) demultiplexer_3 (
    .out0(demultiplexer_3_out0), .out1(demultiplexer_3_out1), .in(multiplexer_2_out), .sel(REVERSE_AMOUNT[2]));  // open: en
  Multiplexer #(.width(32)) multiplexer_3 (
    .in0(demultiplexer_3_out0),
    .in1({demultiplexer_3_out1[27:24], demultiplexer_3_out1[31:28], demultiplexer_3_out1[19:16], demultiplexer_3_out1[23:20], demultiplexer_3_out1[11:8], demultiplexer_3_out1[15:12], demultiplexer_3_out1[3:0], demultiplexer_3_out1[7:4]}),
    .out(multiplexer_3_out), .sel(REVERSE_AMOUNT[2]));  // open: en
  Demultiplexer #(.width(32)) demultiplexer_4 (
    .out0(demultiplexer_4_out0), .out1(demultiplexer_4_out1), .in(multiplexer_3_out), .sel(REVERSE_AMOUNT[3]));  // open: en
  Demultiplexer #(.width(32)) demultiplexer_5 (
    .out0(demultiplexer_5_out0), .out1(demultiplexer_5_out1), .in(multiplexer_4_out), .sel(REVERSE_AMOUNT[4]));  // open: en
  Multiplexer #(.width(32)) multiplexer_4 (
    .in0(demultiplexer_4_out0),
    .in1({demultiplexer_4_out1[23:16], demultiplexer_4_out1[31:24], demultiplexer_4_out1[7:0], demultiplexer_4_out1[15:8]}),
    .out(multiplexer_4_out), .sel(REVERSE_AMOUNT[3]));  // open: en
  Multiplexer #(.width(32)) multiplexer_5 (
    .in0(demultiplexer_5_out0), .in1({demultiplexer_5_out1[15:0], demultiplexer_5_out1[31:16]}),
    .out(OUTPUT), .sel(REVERSE_AMOUNT[4]));  // open: en

  // Notes on the sheet:
  //   1 swap
  //   Feel free to use this component, or not, however you want!
endmodule

module u_LS (
  input  [31:0] x,
  input  [31:0] y,
  output [31:0] out_3
);

  wire [4:0] bit_extender_1_out;
  wire [31:0] shifter_1_out, u_swap_1_out_2;

  Bit_Extender #(.in_width(32), .out_width(5)) bit_extender_1 (.in(y), .out(bit_extender_1_out));
  u_Swap u_swap_1 (.x(x), .out_2(u_swap_1_out_2));
  Shifter #(.width(32), .shift("ar")) shifter_1 (.in(u_swap_1_out_2), .\dist (bit_extender_1_out), .out(shifter_1_out));
  u_Swap u_swap_2 (.x(shifter_1_out), .out_2(out_3));
endmodule

module u_Swap (
  input  [31:0] x,
  output [31:0] out_2
);


  assign out_2 = {x[0], x[1], x[2], x[3], x[4], x[5], x[6], x[7], x[8], x[9], x[10], x[11], x[12], x[13], x[14], x[15], x[16], x[17], x[18], x[19], x[20], x[21], x[22], x[23], x[24], x[25], x[26], x[27], x[28], x[29], x[30], x[31]};
endmodule
