// Logisim project mem-harness.circ as structural Verilog: 1 circuit, main circuit main
module main (
  output [7:0] test_num,
  output [31:0] Data_Mem_Out
);

  wire clock_1_out;
  wire [1:0] rom_3_data;
  wire [7:0] adder_1_out;
  wire [31:0] rom_1_data, rom_2_data;

  Register register_1 (.D(adder_1_out), .en(1'b1), .Q(test_num), .clk(clock_1_out));  // open: clr
  Adder adder_1 (.a(8'h1), .b(test_num), .out(adder_1_out));  // open: cin, cout
  ROM #(.dataWidth(32)) rom_1 (.addr(test_num), .data(rom_1_data));  // open: sel
  ROM #(.dataWidth(32)) rom_2 (.addr(test_num), .data(rom_2_data));  // open: sel
  ROM #(.dataWidth(2)) rom_3 (.addr(test_num), .data(rom_3_data));  // open: sel
  Clock clock_1 (.out(clock_1_out));
  // mem_main main_1: pin names not known; wires that end beside it: rom_1_data, rom_2_data, rom_3_data[1], rom_3_data[0], clock_1_out, Data_Mem_Out

  // Notes on the sheet:
  //   contents of rom_1 (hex, n*v repeats v):
  //   10010004 10010004 10010005 10010006 10010007
  //   contents of rom_2 (hex, n*v repeats v):
  //   80200802 1010101
  //   contents of rom_3 (hex, n*v repeats v):
  //   1 0 2 2 2
endmodule
