// Logisim project ALU-slt.circ as structural Verilog: 1 circuit, main circuit main
module main (
  output [7:0] Test_num,
  output Signed_Overflow,
  output [31:0] Result,
  output Equal,
  output [7:0] Clock_Count,
  output halt
);

  wire clock_1_out;
  wire [5:0] rom_3_data;
  wire [7:0] adder_1_out;
  wire [31:0] rom_1_data, rom_2_data;

  Clock clock_1 (.out(clock_1_out));
  Adder adder_1 (.a(8'h1), .b(Clock_Count), .out(adder_1_out));  // open: cin, cout
  Register register_1 (.D(adder_1_out), .Q(Clock_Count), .clk(clock_1_out));  // open: en, clr
  Comparator comparator_1 (.a(Clock_Count), .b(8'h4), .eq(halt));  // open: gt, lt
  ROM #(.dataWidth(32)) rom_1 (.addr(Clock_Count), .data(rom_1_data));  // open: sel
  ROM #(.dataWidth(32)) rom_2 (.addr(Clock_Count), .data(rom_2_data));  // open: sel
  ROM #(.dataWidth(6)) rom_3 (.addr(Clock_Count), .data(rom_3_data));  // open: sel
  alu_main main_1 (
    .Switch__S(rom_3_data), .X(rom_1_data), .Equal(Equal), .RESULT(Result),
    .Signed_Overflow(Signed_Overflow), .Y(rom_2_data));

  assign Test_num = Clock_Count;

  // Notes on the sheet:
  //   contents of rom_1 (hex, n*v repeats v):
  //   f0f0f0f0 11100000 ffffffff fffffff
  //   contents of rom_2 (hex, n*v repeats v):
  //   0 11110000 0 11111111
  //   contents of rom_3 (hex, n*v repeats v):
  //   2a 2a 2b 2b
  //   YOUR ALU SHOULD FIT HERE
  //   There should be no blue/red wires here, and the result shouldn't be x's.
endmodule
