// Logisim project cpu.circ as structural Verilog: 4 circuits, main circuit main
module main (
  input  [31:0] RS_READ_VALUE,
  input  [31:0] RT_READ_VALUE,
  input  [31:0] INSTRUCTION,
  input  CLOCK,
  input  RESET,
  output [31:0] t0,
  output [31:0] t1,
  output [31:0] t2,
  output [31:0] t3,
  output [4:0] RS,
  output [4:0] RT,
  output [4:0] Write_Register,
  output [31:0] RD_WRITE_VALUE,
  output RD_WRITE_ENABLE,
  output [23:0] FETCH_ADDRESS
);

  wire access_byte, ALU_signed_overflow, ALUSrc, and_2_out, and_3_out, and_4_out, beq, bne, branch_taken,
       check_if_t0_t3_1_if_t0_t3, check_if_t0_t3_2_if_t0_t3, check_if_t0_t3_3_if_t0_t3, comparator_1_eq, eq,
       ExtOp, j, jal, jr, lbu, lui, MemToReg, MemWrite, not_1_out, not_2_out, not_3_out, or_1_out, or_2_out,
       or_4_out, RegDst, RegWrite, shift, write_regfile;
  wire [4:0] multiplexer_5_out;
  wire [5:0] ALUCtr, bit_extender_2_out;
  wire [15:0] imm;
  wire [23:0] adder_1_out, adder_2_out, adder_3_out, bit_extender_1_out, j_addr, jr_addr, multiplexer_2_out,
       multiplexer_3_out, multiplexer_4_out, multiplexer_6_out, old_PC_q;
  wire [31:0] ALU_result, bit_extender_4_out, bit_extender_5_out, bit_extender_6_out, MEM_p6,
       multiplexer_1_out, multiplexer_8_out, multiplexer_9_out, multiplexer_10_out, multiplexer_11_out,
       multiplexer_12_out, multiplexer_13_out, multiplexer_14_out, or_5_out, ra, regfile_wrapper_read_data_1,
       regfile_wrapper_read_data_2, shifter_1_out;
  wire [31:26] register_1_q;

  not not_1 (not_1_out, write_regfile);
  and and_1 (RD_WRITE_ENABLE, not_1_out, RegWrite);
  Multiplexer #(.width(32)) multiplexer_1 (
    .in0(INSTRUCTION), .in1({32{1'b0}}), .out(multiplexer_1_out), .sel(or_2_out));  // open: en
  Comparator #(.width(16)) comparator_1 (.a({16{1'b0}}), .b(imm), .eq(comparator_1_eq));  // open: gt, lt
  not not_2 (not_2_out, comparator_1_eq);
  and and_2 (and_2_out, not_2_out, branch_taken, or_1_out);
  or or_1 (or_1_out, bne, beq);
  or or_2 (or_2_out, and_2_out, jr, jal, j);
  Register #(.width(32)) register_1 (
    .D(multiplexer_1_out), .Q({register_1_q, RS, RT, imm}), .clk(CLOCK));  // open: en, clr
  Multiplexer #(.width(24)) multiplexer_2 (
    .in0(24'h1), .in1({24{1'b0}}), .out(multiplexer_2_out), .sel(or_2_out));  // open: en
  assign bit_extender_1_out = {{8{imm[15]}}, imm};  // Bit_Extender bit_extender_1
  // Probe on {register_1_q, RS, RT, imm}
  not not_3 (not_3_out, eq);
  and and_3 (and_3_out, not_3_out, bne);
  and and_4 (and_4_out, beq, eq);
  Adder #(.width(24)) adder_1 (.a(multiplexer_2_out), .b(FETCH_ADDRESS), .out(adder_1_out));  // open: cin, cout
  or or_3 (branch_taken, and_4_out, and_3_out);
  Adder #(.width(24)) adder_2 (.a(adder_1_out), .b(bit_extender_1_out), .out(adder_2_out));  // open: cin, cout
  Subtractor #(.width(24)) subtractor_1 (.a({RS[2:0], RT, imm}), .b(24'h100000), .out(j_addr));  // open: bin, bout
  Bit_Extender #(.in_width(11), .out_width(6)) bit_extender_2 (.in(imm[10:0]), .out(bit_extender_2_out));
  or or_4 (or_4_out, j, jal);
  Multiplexer #(.width(24)) multiplexer_3 (
    .in0(adder_1_out), .in1(adder_2_out), .out(multiplexer_3_out), .sel(branch_taken));  // open: en
  Multiplexer #(.width(24)) multiplexer_4 (
    .in0(multiplexer_3_out), .in1(j_addr), .out(multiplexer_4_out), .sel(or_4_out));  // open: en
  Register #(.width(24)) old_PC (.D(adder_1_out), .Q(old_PC_q), .clk(CLOCK));  // open: en, clr
  Adder #(.width(24)) adder_3 (.a(old_PC_q), .b(24'h100000), .out(adder_3_out));  // open: cin, cout
  cpu_control cpu_control_1 (
    .opcode(register_1_q), .funct(bit_extender_2_out), .RegDst(RegDst), .ALUSrc(ALUSrc), .shift(shift),
    .lui(lui), .ALUCtr(ALUCtr), .access_byte(access_byte), .MemToReg(MemToReg), .MemWrite(MemWrite),
    .beq(beq), .bne(bne), .j(j), .jal(jal), .jr(jr), .RegWrite(RegWrite), .ExtOp(ExtOp), .lbu(lbu));
  Multiplexer #(.width(5)) multiplexer_5 (
    .in0(RT), .in1(imm[15:11]), .out(multiplexer_5_out), .sel(RegDst));  // open: en
  Multiplexer #(.width(24)) multiplexer_6 (
    .in0(multiplexer_4_out), .in1(jr_addr), .out(multiplexer_6_out), .sel(jr));  // open: en
  assign ra = {{8{1'b0}}, adder_3_out};  // Bit_Extender bit_extender_3
  Multiplexer #(.width(5)) multiplexer_7 (
    .in0(multiplexer_5_out), .in1({5{1'b1}}), .out(Write_Register), .sel(jal));  // open: en
  check_if_t0_t3 check_if_t0_t3_1 (.\reg (Write_Register), .if_t0_t3(check_if_t0_t3_1_if_t0_t3));
  Register #(.width(24)) PC (.D(multiplexer_6_out), .Q(FETCH_ADDRESS), .clk(CLOCK));  // open: en, clr
  and and_5 (write_regfile, check_if_t0_t3_1_if_t0_t3, RegWrite);
  regfile_wrapper regfile_wrapper (
    .read_register_1(RS), .read_register_2(RT), .write_register(Write_Register), .write_data(RD_WRITE_VALUE),
    .t0(t0), .t1(t1), .t2(t2), .t3(t3), .RegWrite(write_regfile), .clock(CLOCK),
    .read_data_1(regfile_wrapper_read_data_1), .read_data_2(regfile_wrapper_read_data_2));
  check_if_t0_t3 check_if_t0_t3_2 (.\reg (RT), .if_t0_t3(check_if_t0_t3_2_if_t0_t3));
  check_if_t0_t3 check_if_t0_t3_3 (.\reg (RS), .if_t0_t3(check_if_t0_t3_3_if_t0_t3));
  Multiplexer #(.width(32)) multiplexer_8 (
    .in0(RS_READ_VALUE), .in1(regfile_wrapper_read_data_1), .out(multiplexer_8_out),
    .sel(check_if_t0_t3_3_if_t0_t3));  // open: en
  Multiplexer #(.width(32)) multiplexer_9 (
    .in0(RT_READ_VALUE), .in1(regfile_wrapper_read_data_2), .out(multiplexer_9_out),
    .sel(check_if_t0_t3_2_if_t0_t3));  // open: en
  assign bit_extender_4_out = {{16{1'b0}}, imm};  // Bit_Extender bit_extender_4
  Multiplexer #(.width(32)) multiplexer_10 (
    .in0(bit_extender_4_out), .in1(bit_extender_5_out), .out(multiplexer_10_out), .sel(ExtOp));  // open: en
  assign bit_extender_5_out = {{16{imm[15]}}, imm};  // Bit_Extender bit_extender_5
  Subtractor #(.width(24)) subtractor_2 (
    .a(multiplexer_8_out[23:0]), .b(24'h100000), .out(jr_addr));  // open: bin, bout
  assign bit_extender_6_out = {{16{1'b0}}, imm};  // Bit_Extender bit_extender_6
  Multiplexer #(.width(32)) multiplexer_11 (
    .in0(multiplexer_9_out), .in1(multiplexer_10_out), .out(multiplexer_11_out), .sel(ALUSrc));  // open: en
  Shifter #(.width(32)) shifter_1 (.in(bit_extender_6_out), .\dist (5'b10000), .out(shifter_1_out));
  alu_main ALU (
    .Switch__S(ALUCtr), .X(multiplexer_8_out), .Equal(eq), .RESULT(ALU_result),
    .Signed_Overflow(ALU_signed_overflow), .Y(multiplexer_11_out));
  // mem_main MEM: pin names not known; wires that end beside it: ALU_result, multiplexer_9_out, access_byte, MemWrite, CLOCK, MEM_p6
  LED overflow (.in(ALU_signed_overflow));
  Multiplexer #(.width(32)) multiplexer_12 (
    .in0(ALU_result), .in1(shifter_1_out), .out(multiplexer_12_out), .sel(lui));  // open: en
  assign or_5_out = MEM_p6 | 32'hffffff00;  // OR_Gate or_5, 32 bits wide
  Multiplexer #(.width(32)) multiplexer_13 (
    .in0(multiplexer_12_out), .in1(multiplexer_14_out), .out(multiplexer_13_out), .sel(MemToReg));  // open: en
  Multiplexer #(.width(32)) multiplexer_14 (
    .in0(MEM_p6), .in1(or_5_out), .out(multiplexer_14_out), .sel(lbu));  // open: en
  Multiplexer #(.width(32)) multiplexer_15 (
    .in0(multiplexer_13_out), .in1(ra), .out(RD_WRITE_VALUE), .sel(jal));  // open: en

  // Other names for the same wires on the sheet: rd[4:0] = imm[15:11]; clk = CLOCK; fetch_addr[23:0] = FETCH_ADDRESS;
  //   run_rs_val[31:0] = RS_READ_VALUE; run_rt_val[31:0] = RT_READ_VALUE; rw[4:0] = Write_Register;
  //   write_val[31:0] = RD_WRITE_VALUE

  // Notes on the sheet:
  //   These are outputs/inputs from run.circ
  //   These are outputs to run.circ
endmodule

module check_if_t0_t3 (
  input  [4:0] \reg ,
  output if_t0_t3
);

  wire comparator_1_lt, comparator_2_gt;

  Comparator #(.width(5), .mode("unsigned")) comparator_1 (
    .a(\reg ), .b(5'b01100), .lt(comparator_1_lt));  // open: gt, eq
  Comparator #(.width(5), .mode("unsigned")) comparator_2 (
    .a(\reg ), .b(5'b00111), .gt(comparator_2_gt));  // open: eq, lt
  and \and  (if_t0_t3, comparator_1_lt, comparator_2_gt);
endmodule

module cpu_control (
  input  [5:0] opcode,
  input  [5:0] funct,
  output RegDst,
  output ALUSrc,
  output shift,
  output lui,
  output [5:0] ALUCtr,
  output access_byte,
  output MemToReg,
  output MemWrite,
  output beq,
  output bne,
  output j,
  output jal,
  output jr,
  output RegWrite,
  output ExtOp,
  output lbu
);

  wire addiu, and_2_out, andi, comparator_14_eq, comparator_15_eq, comparator_16_eq, jr_t, lb, lw, not_1_out,
       or_3_out, or_4_out, or_5_out, or_6_out, ori;

  and and_1 (jr, RegDst, jr_t);
  Comparator #(.width(6), .mode("unsigned")) comparator_1 (.a({6{1'b0}}), .b(opcode), .eq(RegDst));  // open: gt, lt
  Comparator #(.width(6), .mode("unsigned")) comparator_2 (.a(6'b001001), .b(opcode), .eq(addiu));  // open: gt, lt
  Comparator #(.width(6), .mode("unsigned")) comparator_3 (.a(6'b001100), .b(opcode), .eq(andi));  // open: gt, lt
  Comparator #(.width(6), .mode("unsigned")) comparator_4 (.a(6'b001101), .b(opcode), .eq(ori));  // open: gt, lt
  Comparator #(.width(6), .mode("unsigned")) comparator_5 (.a(6'b001111), .b(opcode), .eq(lui));  // open: gt, lt
  Comparator #(.width(6), .mode("unsigned")) comparator_6 (.a(6'b100000), .b(opcode), .eq(lb));  // open: gt, lt
  Comparator #(.width(6), .mode("unsigned")) comparator_7 (.a(6'b100100), .b(opcode), .eq(lbu));  // open: gt, lt
  Comparator #(.width(6), .mode("unsigned")) comparator_8 (.a(6'b100011), .b(opcode), .eq(lw));  // open: gt, lt
  Comparator #(.width(6), .mode("unsigned")) comparator_9 (.a(6'b101011), .b(opcode), .eq(MemWrite));  // open: gt, lt
  Comparator #(.width(6), .mode("unsigned")) comparator_10 (.a(6'b000100), .b(opcode), .eq(beq));  // open: gt, lt
  Comparator #(.width(6), .mode("unsigned")) comparator_11 (.a(6'b000101), .b(opcode), .eq(bne));  // open: gt, lt
  Comparator #(.width(6), .mode("unsigned")) comparator_12 (.a(6'b000010), .b(opcode), .eq(j));  // open: gt, lt
  Comparator #(.width(6), .mode("unsigned")) comparator_13 (.a(6'b000011), .b(opcode), .eq(jal));  // open: gt, lt
  nor nor_1 (RegWrite, jr, j, MemWrite, beq, bne);
  nor nor_2 (ExtOp, andi, ori);
  or or_1 (access_byte, lb, lbu);
  or or_2 (MemToReg, lb, lbu, lw);
  nor nor_3 (ALUSrc, RegDst, beq, bne);
  not not_1 (not_1_out, jr_t);
  assign ALUCtr = and_2_out ? funct : 6'bz;  // Controlled_Buffer controlled_buffer_1
  and and_2 (and_2_out, RegDst, not_1_out);
  assign ALUCtr = or_3_out ? 6'b100001 : 6'bz;  // Controlled_Buffer controlled_buffer_2
  or or_3 (or_3_out, lb, lbu, lw, MemWrite, addiu);
  assign ALUCtr = andi ? 6'b100100 : 6'bz;  // Controlled_Buffer controlled_buffer_3
  assign ALUCtr = or_4_out ? 6'b100101 : 6'bz;  // Controlled_Buffer controlled_buffer_4
  or or_4 (or_4_out, ori, j, jal);
  assign ALUCtr = or_5_out ? 6'b100011 : 6'bz;  // Controlled_Buffer controlled_buffer_5
  or or_5 (or_5_out, beq, bne);
  Comparator #(.width(6), .mode("unsigned")) comparator_14 (
    .a({6{1'b0}}), .b(funct), .eq(comparator_14_eq));  // open: gt, lt
  Comparator #(.width(6), .mode("unsigned")) comparator_15 (
    .a(6'b000010), .b(funct), .eq(comparator_15_eq));  // open: gt, lt
  Comparator #(.width(6), .mode("unsigned")) comparator_16 (
    .a(6'b000011), .b(funct), .eq(comparator_16_eq));  // open: gt, lt
  Comparator #(.width(6), .mode("unsigned")) comparator_17 (.a(6'b001000), .b(funct), .eq(jr_t));  // open: gt, lt
  and and_3 (shift, RegDst, or_6_out);
  or or_6 (or_6_out, comparator_14_eq, comparator_15_eq, comparator_16_eq);

  // Other names for the same wires on the sheet: R = RegDst; sw = MemWrite
endmodule

module regfile_wrapper (
  input  [4:0] read_register_1,
  input  [4:0] read_register_2,
  input  [4:0] write_register,
  input  RegWrite,
  input  clock,
  input  [31:0] write_data,
  output [31:0] t0,
  output [31:0] t1,
  output [31:0] t2,
  output [31:0] t3,
  output [31:0] read_data_1,
  output [31:0] read_data_2
);

  wire [1:0] bit_extender_1_out, bit_extender_2_out, bit_extender_3_out;

  Bit_Extender #(.in_width(5), .out_width(2)) bit_extender_1 (.in(read_register_1), .out(bit_extender_1_out));
  Bit_Extender #(.in_width(5), .out_width(2)) bit_extender_2 (.in(read_register_2), .out(bit_extender_2_out));
  Bit_Extender #(.in_width(5), .out_width(2)) bit_extender_3 (.in(write_register), .out(bit_extender_3_out));
  regfile_main regfile (
    .Read_register_1(bit_extender_1_out), .Read_register_2(bit_extender_2_out),
    .write_register(bit_extender_3_out), .write_data(write_data), .t0_Value(t0), .t1_Value(t1),
    .t2_Value(t2), .t3_Value(t3), .RegWrite(RegWrite), .clock(clock), .Read_Data_1(read_data_1),
    .Read_Data_2(read_data_2));

  // Notes on the sheet:
  //   regfile wrapper whose register inputs are 5 bits rather than 2 bits
endmodule
