// Logisim project regfile.circ as structural Verilog: 1 circuit, main circuit main
module main (
  input  [1:0] Read_register_1,
  input  [1:0] Read_register_2,
  input  [1:0] write_register,
  input  [31:0] write_data,
  input  RegWrite,
  input  clock,
  output [31:0] t0_Value,
  output [31:0] t1_Value,
  output [31:0] t2_Value,
  output [31:0] t3_Value,
  output [31:0] Read_Data_1,
  output [31:0] Read_Data_2
);

  wire and_1_out, and_2_out, and_3_out, and_4_out, reg_t0_write, reg_t1_write, reg_t2_write, reg_t3_write;
  wire [31:0] multiplexer_1_out, multiplexer_2_out, multiplexer_3_out, multiplexer_4_out;

  Demultiplexer #(.select(2)) demultiplexer_1 (
    .out0(reg_t0_write), .out1(reg_t1_write), .out2(reg_t2_write), .out3(reg_t3_write), .in(1'b1),
    .sel(write_register));  // open: en
  Multiplexer #(.width(32)) multiplexer_1 (
    .in0(t0_Value), .in1(write_data), .out(multiplexer_1_out), .sel(and_1_out));  // open: en
  and and_1 (and_1_out, RegWrite, reg_t0_write);
  Multiplexer #(.width(32)) multiplexer_2 (
    .in0(t1_Value), .in1(write_data), .out(multiplexer_2_out), .sel(and_2_out));  // open: en
  and and_2 (and_2_out, RegWrite, reg_t1_write);
  Multiplexer #(.width(32)) multiplexer_3 (
    .in0(t2_Value), .in1(write_data), .out(multiplexer_3_out), .sel(and_3_out));  // open: en
  and and_3 (and_3_out, RegWrite, reg_t2_write);
  Multiplexer #(.width(32)) multiplexer_4 (
    .in0(t3_Value), .in1(write_data), .out(multiplexer_4_out), .sel(and_4_out));  // open: en
  and and_4 (and_4_out, RegWrite, reg_t3_write);
  Register #(.width(32)) t0 (.D(multiplexer_1_out), .Q(t0_Value), .clk(clock));  // open: en, clr
  Register #(.width(32)) t1 (.D(multiplexer_2_out), .Q(t1_Value), .clk(clock));  // open: en, clr
  Register #(.width(32)) t2 (.D(multiplexer_3_out), .Q(t2_Value), .clk(clock));  // open: en, clr
  Register #(.width(32)) t3 (.D(multiplexer_4_out), .Q(t3_Value), .clk(clock));  // open: en, clr
  Multiplexer #(.select(2), .width(32)) multiplexer_5 (
    .in0(t0_Value), .in1(t1_Value), .in2(t2_Value), .in3(t3_Value), .out(Read_Data_1), .sel(Read_register_1));  // open: en
  Multiplexer #(.select(2), .width(32)) multiplexer_6 (
    .in0(t0_Value), .in1(t1_Value), .in2(t2_Value), .in3(t3_Value), .out(Read_Data_2), .sel(Read_register_2));  // open: en

  // Other names for the same wires on the sheet: reg_clock = clock; reg_read1[1:0] = Read_register_1;
  //   reg_read2[1:0] = Read_register_2; reg_t0_out[31:0] = t0_Value; reg_t1_out[31:0] = t1_Value;
  //   reg_t2_out[31:0] = t2_Value; reg_t3_out[31:0] = t3_Value; reg_wrie_data[31:0] = write_data;
  //   reg_write_reg[1:0] = write_register

  // Notes on the sheet:
  //   These are INPUTS to the circuit
  //   These are INPUTS to the circuit
  //   DO NOT CHANGE THE LOCATIONS OF THE INPUTS/OUTPUTS! IF YOU DO SO, YOU NEED TO MAKE SURE THE PINS ARE AT THE RIGHT PLACE!
  //   These are OUTPUTS to the circuit
  //   Yet again, the clock is not an actual clock, but an input, one that will be driven from a higher circuit
  //   These are OUTPUTS to the circuit
endmodule
